// Logisim project 4bit_calc.circ as structural Verilog: 1 circuit, main circuit main
module main (
);

  wire ABSTRACT_out, and_1_out, and_2_out, and_3_out, and_4_out, and_5_out, and_6_out, and_7_out, and_8_out,
       and_9_out, and_10_out, and_11_out, and_12_out, and_13_out, and_14_out, and_15_out, and_16_out,
       and_17_out, and_18_out, and_19_out, and_20_out, and_21_out, and_22_out, and_23_out, and_24_out,
       and_25_out, and_26_out, and_27_out, and_28_out, and_29_out, and_30_out, and_31_out, and_32_out,
       and_33_out, and_34_out, and_35_out, and_36_out, and_37_out, and_38_out, d_ff_1_q, d_ff_2_q, d_ff_3_q,
       d_ff_4_q, N0_out, N1_out, N2_out, N3_out, N4_out, N5_out, N6_out, N7_out, N8_out, N9_out, not_1_out,
       not_2_out, not_3_out, not_4_out, not_5_out, not_6_out, not_7_out, not_8_out, not_9_out, not_10_out,
       not_11_out, not_12_out, not_13_out, not_14_out, not_15_out, not_16_out, not_17_out, not_18_out,
       not_19_out, not_20_out, not_21_out, not_22_out, not_23_out, not_24_out, not_25_out, not_26_out,
       not_27_out, not_28_out, not_29_out, not_30_out, not_31_out, not_32_out, not_33_out, not_34_out,
       not_35_out, not_36_out, or_1_out, or_2_out, or_3_out, or_4_out, or_5_out, or_6_out, or_7_out,
       or_8_out, or_9_out, or_10_out, or_11_out, or_12_out, or_13_out, or_14_out, or_15_out, or_16_out,
       or_17_out, or_18_out, or_19_out, or_20_out, or_21_out, or_22_out, or_23_out, or_24_out, or_25_out,
       or_26_out, or_27_out, RESET_out, t_ff_1_q, t_ff_1_qn, t_ff_2_q, t_ff_3_q, t_ff_4_q, t_ff_5_q,
       t_ff_6_q, xor_1_out, xor_2_out, xor_3_out, xor_4_out, xor_5_out, xor_6_out, xor_7_out, xor_8_out,
       xor_9_out, xor_10_out, xor_11_out, xor_12_out;

  Button ABSTRACT (.out(ABSTRACT_out));
  Button RESET (.out(RESET_out));
  or or_1 (or_1_out, or_2_out, or_3_out);
  Button N0 (.out(N0_out));
  Button N1 (.out(N1_out));
  Button N2 (.out(N2_out));
  Button N3 (.out(N3_out));
  Button N4 (.out(N4_out));
  Button N5 (.out(N5_out));
  Button N6 (.out(N6_out));
  Button N7 (.out(N7_out));
  Button N8 (.out(N8_out));
  Button N9 (.out(N9_out));
  or or_2 (or_2_out, or_5_out, or_6_out);
  or or_3 (or_3_out, or_7_out, or_8_out);
  or or_4 (or_4_out, or_1_out, N0_out);
  not not_1 (not_1_out, or_4_out);
  and and_1 (and_1_out, or_4_out, not_1_out);
  T_Flip_Flop t_ff_1 (.T(or_4_out), .clk(and_1_out), .Q(t_ff_1_q), .Qn(t_ff_1_qn), .reset(RESET_out));  // open: preset
  or or_5 (or_5_out, N1_out, N5_out, N7_out, N9_out, N3_out);
  or or_6 (or_6_out, N2_out, N3_out, N6_out, N7_out);
  or or_7 (or_7_out, N4_out, N5_out, N6_out, N7_out);
  or or_8 (or_8_out, N8_out, N9_out);
  and and_2 (and_2_out, or_5_out, t_ff_1_qn);
  and and_3 (and_3_out, or_6_out, t_ff_1_qn);
  and and_4 (and_4_out, or_7_out, t_ff_1_qn);
  and and_5 (and_5_out, or_8_out, t_ff_1_qn);
  not not_2 (not_2_out, ABSTRACT_out);
  and and_6 (and_6_out, not_2_out, ABSTRACT_out);
  T_Flip_Flop t_ff_2 (.T(ABSTRACT_out), .clk(and_6_out), .Q(t_ff_2_q), .reset(RESET_out));  // open: Qn, preset
  T_Flip_Flop t_ff_3 (.T(and_2_out), .clk(and_1_out), .Q(t_ff_3_q), .reset(RESET_out));  // open: Qn, preset
  T_Flip_Flop t_ff_4 (.T(and_3_out), .clk(and_1_out), .Q(t_ff_4_q), .reset(RESET_out));  // open: Qn, preset
  T_Flip_Flop t_ff_5 (.T(and_4_out), .clk(and_1_out), .Q(t_ff_5_q), .reset(RESET_out));  // open: Qn, preset
  T_Flip_Flop t_ff_6 (.T(and_5_out), .clk(and_1_out), .Q(t_ff_6_q), .reset(RESET_out));  // open: Qn, preset
  and and_7 (and_7_out, or_5_out, t_ff_1_q);
  and and_8 (and_8_out, or_6_out, t_ff_1_q);
  and and_9 (and_9_out, or_7_out, t_ff_1_q);
  and and_10 (and_10_out, or_8_out, t_ff_1_q);
  D_Flip_Flop d_ff_1 (.D(and_7_out), .clk(and_1_out), .Q(d_ff_1_q), .reset(RESET_out));  // open: Qn, preset
  D_Flip_Flop d_ff_2 (.D(and_8_out), .clk(and_1_out), .Q(d_ff_2_q), .reset(RESET_out));  // open: Qn, preset
  D_Flip_Flop d_ff_3 (.D(and_9_out), .clk(and_1_out), .Q(d_ff_3_q), .reset(RESET_out));  // open: Qn, preset
  D_Flip_Flop d_ff_4 (.D(and_10_out), .clk(and_1_out), .Q(d_ff_4_q), .reset(RESET_out));  // open: Qn, preset
  xor xor_1 (xor_1_out, d_ff_1_q, t_ff_2_q);
  xor xor_2 (xor_2_out, d_ff_2_q, t_ff_2_q);
  xor xor_3 (xor_3_out, d_ff_3_q, t_ff_2_q);
  xor xor_4 (xor_4_out, d_ff_4_q, t_ff_2_q);
  xor xor_5 (xor_5_out, t_ff_3_q, xor_1_out);
  and and_11 (and_11_out, t_ff_3_q, xor_1_out);
  xor xor_6 (xor_6_out, t_ff_4_q, xor_2_out);
  and and_12 (and_12_out, t_ff_4_q, xor_2_out);
  xor xor_7 (xor_7_out, t_ff_5_q, xor_3_out);
  and and_13 (and_13_out, t_ff_5_q, xor_3_out);
  xor xor_8 (xor_8_out, t_ff_6_q, xor_4_out);
  and and_14 (and_14_out, t_ff_6_q, xor_4_out);
  and and_15 (and_15_out, t_ff_2_q, xor_5_out);
  and and_16 (and_16_out, xor_5_out, t_ff_2_q, xor_6_out);
  and and_17 (and_17_out, xor_6_out, and_11_out);
  and and_18 (and_18_out, xor_5_out, xor_6_out, xor_7_out, t_ff_2_q);
  and and_19 (and_19_out, xor_6_out, xor_7_out, and_11_out);
  and and_20 (and_20_out, xor_7_out, and_12_out);
  LED led_1 (.in(and_11_out));
  LED led_2 (.in(and_12_out));
  LED led_3 (.in(and_13_out));
  or or_9 (or_9_out, and_15_out, and_11_out);
  or or_10 (or_10_out, and_16_out, and_12_out, and_17_out);
  or or_11 (or_11_out, and_18_out, and_19_out, and_20_out, and_13_out);
  and and_21 (and_21_out, xor_8_out, or_11_out);
  or or_12 (or_12_out, and_21_out, and_14_out);
  not not_3 (not_3_out, t_ff_2_q);
  xor xor_9 (xor_9_out, t_ff_2_q, xor_5_out);
  xor xor_10 (xor_10_out, or_9_out, xor_6_out);
  xor xor_11 (xor_11_out, or_10_out, xor_7_out);
  xor xor_12 (xor_12_out, or_11_out, xor_8_out);
  and and_22 (and_22_out, or_12_out, not_3_out);
  LED led_4 (.in(and_22_out));
  not not_4 (not_4_out, xor_9_out);
  not not_5 (not_5_out, xor_10_out);
  not not_6 (not_6_out, xor_9_out);
  not not_7 (not_7_out, xor_10_out);
  not not_8 (not_8_out, xor_11_out);
  not not_9 (not_9_out, xor_11_out);
  not not_10 (not_10_out, xor_12_out);
  not not_11 (not_11_out, xor_10_out);
  not not_12 (not_12_out, xor_11_out);
  not not_13 (not_13_out, xor_12_out);
  not not_14 (not_14_out, xor_9_out);
  not not_15 (not_15_out, xor_11_out);
  not not_16 (not_16_out, xor_11_out);
  not not_17 (not_17_out, xor_12_out);
  not not_18 (not_18_out, xor_9_out);
  not not_19 (not_19_out, xor_10_out);
  not not_20 (not_20_out, xor_12_out);
  not not_21 (not_21_out, xor_10_out);
  not not_22 (not_22_out, xor_12_out);
  not not_23 (not_23_out, xor_9_out);
  not not_24 (not_24_out, xor_12_out);
  not not_25 (not_25_out, xor_12_out);
  not not_26 (not_26_out, xor_10_out);
  not not_27 (not_27_out, xor_11_out);
  not not_28 (not_28_out, xor_11_out);
  not not_29 (not_29_out, xor_9_out);
  not not_30 (not_30_out, xor_11_out);
  not not_31 (not_31_out, xor_10_out);
  not not_32 (not_32_out, xor_9_out);
  not not_33 (not_33_out, xor_10_out);
  not not_34 (not_34_out, xor_9_out);
  not not_35 (not_35_out, xor_12_out);
  and and_23 (and_23_out, not_4_out, not_5_out, not_9_out, not_10_out);
  and and_24 (and_24_out, xor_9_out, not_11_out, not_12_out, not_13_out);
  and and_25 (and_25_out, not_14_out, xor_10_out, not_15_out, not_35_out);
  and and_26 (and_26_out, xor_9_out, xor_10_out, not_16_out, not_17_out);
  and and_27 (and_27_out, not_18_out, not_19_out, xor_11_out, not_20_out);
  and and_28 (and_28_out, xor_9_out, not_21_out, xor_11_out, not_22_out);
  and and_29 (and_29_out, not_23_out, xor_10_out, xor_11_out, not_24_out);
  and and_30 (and_30_out, xor_9_out, xor_10_out, xor_11_out, not_25_out);
  and and_31 (and_31_out, not_6_out, not_7_out, not_8_out, xor_12_out);
  and and_32 (and_32_out, xor_9_out, not_26_out, not_27_out, xor_12_out);
  and and_33 (and_33_out, xor_12_out, not_28_out, xor_10_out, not_29_out);
  and and_34 (and_34_out, xor_12_out, not_30_out, xor_10_out, xor_9_out);
  and and_35 (and_35_out, xor_12_out, xor_11_out, not_31_out, not_32_out);
  and and_36 (and_36_out, xor_12_out, xor_11_out, not_33_out, xor_9_out);
  and and_37 (and_37_out, xor_12_out, xor_11_out, xor_10_out, not_34_out);
  and and_38 (and_38_out, xor_12_out, xor_11_out, xor_10_out, xor_9_out);
  or or_13 (or_13_out, and_38_out, and_37_out, and_36_out, and_35_out, and_34_out, and_33_out);
  not not_36 (not_36_out, or_13_out);
  LED led_5 (.in(not_36_out));
  LED led_6 (.in(not_36_out));
  LED led_7 (.in(not_36_out));
  LED led_8 (.in(not_36_out));
  LED led_9 (.in(not_36_out));
  LED led_10 (.in(not_36_out));
  LED led_11 (.in(not_36_out));
  LED led_12 (.in(not_36_out));
  LED led_13 (.in(not_36_out));
  LED led_14 (.in(1'b1));
  LED led_15 (.in(1'b1));
  LED led_16 (.in(1'b1));
  LED led_17 ();  // open: in
  LED led_18 ();  // open: in
  LED led_19 ();  // open: in
  LED led_20 (.in(1'b1));
  LED led_21 (.in(1'b1));
  LED led_22 (.in(1'b1));
  LED led_23 (.in(not_36_out));
  LED led_24 (.in(not_36_out));
  LED led_25 (.in(not_36_out));
  or or_14 (or_14_out, and_32_out, and_31_out, and_30_out, and_29_out, and_28_out, and_26_out, and_25_out, and_23_out);
  or or_15 (or_15_out, and_38_out, and_36_out, and_35_out, and_33_out, or_14_out);
  LED led_26 (.in(or_15_out));
  LED led_27 (.in(or_25_out));
  LED led_28 (.in(or_25_out));
  LED led_29 (.in(or_25_out));
  LED led_30 (.in(or_27_out));
  LED led_31 (.in(or_23_out));
  LED led_32 (.in(or_23_out));
  LED led_33 (.in(or_23_out));
  LED led_34 (.in(or_21_out));
  or or_16 (or_16_out, and_32_out, and_31_out, and_30_out, and_27_out, and_26_out, and_25_out, and_24_out, and_23_out);
  or or_17 (or_17_out, and_37_out, and_36_out, and_35_out, and_34_out, and_33_out, or_16_out);
  LED led_35 (.in(or_15_out));
  LED led_36 (.in(or_15_out));
  LED led_37 (.in(or_17_out));
  LED led_38 (.in(or_17_out));
  LED led_39 (.in(or_17_out));
  LED led_40 (.in(or_27_out));
  LED led_41 (.in(or_27_out));
  LED led_42 (.in(or_19_out));
  LED led_43 (.in(or_19_out));
  LED led_44 (.in(or_19_out));
  LED led_45 (.in(or_21_out));
  LED led_46 (.in(or_21_out));
  or or_18 (or_18_out, and_32_out, and_31_out, and_30_out, and_29_out, and_28_out, and_27_out, and_26_out, and_24_out, and_23_out);
  or or_19 (or_19_out, and_38_out, and_33_out, and_37_out, and_36_out, and_34_out, or_18_out);
  or or_20 (or_20_out, and_32_out, and_31_out, and_29_out, and_28_out, and_26_out, and_25_out, and_23_out);
  or or_21 (or_21_out, and_38_out, and_36_out, and_35_out, and_33_out, or_20_out);
  or or_22 (or_22_out, and_31_out, and_29_out, and_25_out, and_23_out);
  or or_23 (or_23_out, and_35_out, and_33_out, or_22_out);
  or or_24 (or_24_out, and_32_out, and_31_out, and_29_out, and_28_out, and_27_out, and_23_out);
  or or_25 (or_25_out, and_38_out, and_37_out, and_33_out, or_24_out);
  or or_26 (or_26_out, and_32_out, and_31_out, and_29_out, and_28_out, and_27_out, and_26_out, and_25_out);
  or or_27 (or_27_out, and_38_out, and_37_out, and_36_out, and_35_out, and_33_out, or_26_out);

  // Notes on the sheet:
  //   ACTION
  //   ENCODER
  //   BIT 1
  //   BIT 2
  //   BIT 3
  //   BIT 4
  //   1ST NUMBER MEMORY
  //   A0
  //   A1
  //   A2
  //   A3
  //   2ND NUMBER MEMORY
  //   B0
  //   B1
  //   B2
  //   B3
  //   P1
  //   G1
  //   P2
  //   G2
  //   P3
  //   G3
  //   P4
  //   G4
  //   P4
  //   G4
  //   P1
  //   G1
  //   P2
  //   G2
  //   P3
  //   G3
  //   CARRY PREDICTION
  //   C1
  //   C2
  //   C3
  //   C0
  //   OVERFLOW
  //   NUMBER DECODER
  //   0
  //   1
  //   2
  //   3
  //   4
  //   5
  //   6
  //   7
  //   8
  //   9
  //   10
  //   11
  //   12
  //   13
  //   14
  //   15
  //   f
  //   e
  //   a
  //   g
  //   d
  //   a
  //   b
  //   f
  //   c
  //   e
  //   b
  //   a
  //   g
  //   d
  //   c
  //   b
  //   c
  //   d
  //   e
  //   DISPLAY LOGIC
  //   f
  //   g
endmodule
